# Fritzing sketch Светофор (saved by Fritzing 0.9.3b)
breadboards: 1

parts:
  Часть1 = Arduino Pro Mini v13
  LED1 = LEDs [package=led10mm]
  LED2 = LEDs [package=led10mm]
  LED3 = LEDs [package=led10mm]

nets:
  N1: Часть1.GND, LED1.C, LED2.C, LED3.C
  N2: Часть1.D4, LED1.A
  N3: Часть1.D3_PWM, LED2.A
  N4: Часть1.D2, LED3.A
